# Fritzing sketch Circuit Diagram (saved by Fritzing 0.9.3b)
circuit board: 8.46667cm x 5.64444cm

parts:
  Part1 = Arduino Uno (Rev3) - ICSP
  M4 = DC Motor
  S1 = H-Bridge with L298N
  M5 = DC Motor
  M6 = DC Motor
  M7 = DC Motor
  Part3 = Bluetooth HC-05 Macho
  Mod1 = KY-022 Infrared Receiver Module [package="Breakout board"]
  HC-SR04_Sensor_1 = HC-SR04 Ultrasonic Distance Sensor
  M8 = fc-51 [package=THT]
  M9 = fc-51 [package=THT]
  VCC1 = Battery
  Part4 = Arduino Nano (Rev3.0) (ICSP)
  DHT1 = Humidity and Temperature Sensor DHT11
  J3 = Piezo Speaker
  S2 = KY-026
  S3 = 5-channel flame detector module
  J4 = Basic Servo
  LCD2 = LCD screen

nets:
  N1: Part1.A0, M9.pin1
  N2: Part1.A1, M8.pin2
  N3: Part1.A2, HC-SR04_Sensor_1.ECHO
  N4: Part1.A3, HC-SR04_Sensor_1.TRIG
  N5: Part1.A4/SDA, J4.pulse
  N6: Part1.A5/SCL, Mod1.S
  N7: Part1.5V, M8.pin3, M9.pin3
  N8: Part1.D8, S1.IN2
  N9: Part1.D9_PWM, S1.IN1
  N10: Part1.D10_PWM/SS, S1.ENA
  N11: Part1.D2, Part3.TXD
  N12: Part1.D3_PWM, Part3.RXD
  N13: Part1.D5_PWM, S1.ENB
  N14: Part1.D6_PWM, S1.IN4
  N15: Part1.D7, S1.IN3
  GND: Part1.GND, Part3.GND, Mod1.-
  N16: M4.pin_1, S1.M1-02, M7.pin_1
  N17: M4.pin_2, S1.M1-01, M7.pin_2
  N18: S1.12V, VCC1.+
  N19: S1.GND, VCC1.-
  N20: S1.M2-01, M5.pin_2, M6.pin_2
  N21: S1.M2-02, M5.pin_1, M6.pin_1
  VIN: Mod1.Vin, HC-SR04_Sensor_1.VCC
  N22: Part4.GND, DHT1.GND_1
  N23: Part4.D2, LCD2.DB7
  N24: Part4.D3, LCD2.DB6
  N25: Part4.D4, LCD2.DB5
  N26: Part4.D5, LCD2.DB4
  N27: Part4.D7, DHT1.Data-signal
  N28: Part4.D8, S2.pin4
  N29: Part4.D9, J3.pin2
  N30: Part4.D10, S3.pin13
  N31: Part4.D11/MOSI, LCD2.E
  N32: Part4.D12/MISO, LCD2.RS
  5V: Part4.5V, DHT1.Vcc, S2.pin3, S3.pin3, S3.pin4
  N33: S2.pin2, S3.pin1

custom parts:
  H-Bridge with L298N: h-bridge
  KY-022 Infrared Receiver Module: KY-022 IR receiver module, reacts to 38kHz infrared light.
  Humidity and Temperature Sensor DHT11: Digital relative humidity & temperature sensor DHT11
  KY-026: ky-026 flame sensor module
